# Fritzing sketch esquema-arduino (saved by Fritzing 0.9.3b)
breadboards: 1

parts:
  LED1 = LED - 3mm [color="Red (633nm)" package="3 mm [THT]"]  # not connected
  R1 = Photocell (LDR) [package=THT]  # not connected
  S2 = SPST Switch [package=switch-spdt_kit]
  Part1 = Bluetooth HC-05 Macho
  Part2 = Arduino Nano (Rev3.0)
  R2 = Temperature Sensor (Thermistor) [thermistor_type=NTC package=THT]
  R3 = Resistor [tolerance=±5% resistance=100k package=THT]

nets:
  VCC: S2.O, S2.P, Part1.VCC, Part2.5V, R2.pin_1
  N1: S2.S, Part2.D2
  N2: Part1.State, Part2.AREF
  N3: Part1.TXD, Part2.D10
  N4: Part1.RXD, Part2.D11/MOSI
  GND: Part1.GND, Part2.GND, R3.Pin_1
  N5: Part2.A3, R2.pin_0
